# Fritzing sketch HIDKnob_fritzing (saved by Fritzing 0.9.3b)
circuit board: 8.46667cm x 5.64444cm
breadboards: 1

parts:
  Pro_Micro1 = SparkFun Pro Micro
  S1 = Toggle Switch [package=THT]
  S2 = Toggle Switch [package=THT]
  LED1 = LED - 5mm [color="Red (633nm)" package="5 mm [THT]"]
  LED2 = LED - 5mm [color="Red (633nm)" package="5 mm [THT]"]
  3LED_Rotary_Encoder_DIP1 = 3 LED & RE & SW DIP [package=DIP]
  Part1 = 12 NeoPixel Ring [part_number=1643]
  R1 = Resistor [tolerance=±5% resistance=10k package=THT]
  R2 = Resistor [tolerance=±5% resistance=10k package=THT]
  R3 = Resistor [tolerance=±5% resistance=220 package=THT]
  R4 = Resistor [tolerance=±5% resistance=220 package=THT]

nets:
  GND: Pro_Micro1.GND, 3LED_Rotary_Encoder_DIP1.GND, Part1.GND, R1.Pin_1, R2.Pin_1, R3.Pin_1, R4.Pin_1
  N1: Pro_Micro1.2, 3LED_Rotary_Encoder_DIP1.ENC_B
  N2: Pro_Micro1.3, Pro_Micro1.4, 3LED_Rotary_Encoder_DIP1.ENC_A
  N3: Pro_Micro1.5, LED2.anode
  N4: Pro_Micro1.6, LED1.anode
  N5: Pro_Micro1.7, S2.L2, R1.Pin_0
  N6: Pro_Micro1.8, S1.L2, R2.Pin_0
  N7: Pro_Micro1.10, Part1.IN
  N8: Pro_Micro1.15, 3LED_Rotary_Encoder_DIP1.SWITCH
  VCC: Pro_Micro1.VCC, S1.COM, S2.COM, 3LED_Rotary_Encoder_DIP1.VCC, Part1.VDD
  N9: LED1.cathode, R3.Pin_0
  N10: LED2.cathode, R4.Pin_0

custom parts:
  SparkFun Pro Micro: The Pro Micro is similar to the Pro Mini except with an ATmega32U4 on board. The USB transceiver inside the 32U4 allows us to add USB connectivity on-board and do away with bulky external USB interface. Based on: https://github.com/unorthodox-engineers/unorthodox-arduino/blob/master/Unorthodox/fritzing/parts/Pro%20Micro.fzpz
  3 LED & RE & SW DIP: RGB color LED and Rotary Encoder with Switch on PCB board. LED and SW are anode common.
  12 NeoPixel Ring: 12 ultra bright smart LED NeoPixels are arranged in a circle with 1.5" (37mm) outer diameter. The rings are 'chainable' - connect the output pin of one to the input pin of another. Use only one microcontroller pin to control as many as you can chain together! Each LED is addressable as the driver chip is inside the LED. Each one has ~18mA constant current drive so the color will be very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
